# Fritzing sketch ESP06 (saved by Fritzing 0.9.3b)
circuit board: 3.88288cm x 3.74367cm
breadboards: 1

parts:
  J1 = female pin header, 2 pins [form="♀ (female)"]
  R6 = Resistor [tolerance=±5% resistance=10k package="1206 [SMD]"]
  R5 = Resistor [tolerance=±5% resistance=4.7k package="1206 [SMD]"]
  R4 = Resistor [tolerance=±5% resistance=2.2k package="1206 [SMD]"]
  R3 = Resistor [tolerance=±5% resistance=4.7k package="1206 [SMD]"]
  R2 = Resistor [tolerance=±5% resistance=4.7k package="1206 [SMD]"]
  R1 = Resistor [tolerance=±5% resistance=4.7k package="1206 [SMD]"]
  IC1 = Voltage Regulator LM1117 [part_number=TS1117BCW package=sot223]
  J5 = female pin header, 3 pins [form="♀ (female)"]
  J6 = female pin header, 6 pins [form="♀ (female)"]
  J3 = male pin header, 3 pins [form="♂ (male)" part_number="rst / flash"]
  U1 = ESP8266 WiFi Module [part_number=ESP12f]
  C4 = SMD Capacitor [package=1206]
  C5 = SMD Capacitor [package=1206]
  C1 = Electrolytic Capacitor [capacitance=0.47mF package="100 mil [THT, electrolytic]"]

nets:
  5V: J1.pin1, IC1.IN, J6.pin4, C5.1
  GND: J1.pin2, R6.Pin_0, IC1.ADJ, J5.pin1, J6.pin1, J3.pin2, U1.GND, U1.GPIO_15, C4.2, C5.2, C1.-
  GPIO1 -> ECHO: R6.Pin_1, R5.Pin_0, U1.TXD
  N1: R5.Pin_1, J6.pin2
  3.3V: R4.Pin_0, R3.Pin_0, R2.Pin_0, R1.Pin_0, IC1.OUT, J5.pin3, J6.pin6, U1.VCC, U1.CH_PD, C4.1, C1.+
  ONE WIRE: R4.Pin_1, J5.pin2, J6.pin5, U1.GPIO_5
  N2: R3.Pin_1, U1.GPIO_0
  N3: R2.Pin_1, J3.pin3, U1.GPIO_2
  N4: R1.Pin_1, J3.pin1, U1.REST
  GPIO3 -> TRIG: J6.pin3, U1.RXD

notes:
  ESP06
  5V
  echo
  trig
  GND
  3.3V
  1w
  gnd
  rst
  flash

custom parts:
  SMD Capacitor: Capacitor Standard 0603 ceramic capacitor, and 0.1 leaded capacitor.
